# Fritzing sketch controle_real_time (saved by Fritzing 0.9.4)
breadboards: 1

parts:
  ESP32_-_Back1 = ESP32 - CAM
  Componente1 = FTDI Basic Programmer
  LED1 = LED - 5mm [color="Red (633nm)" package="5 mm [THT]"]
  R1 = Resistor [tolerance=±5% resistance=330 package=THT]
  LED2 = LED - 5mm [color="Green (570nm)" package="5 mm [THT]"]
  R2 = Resistor [tolerance=±5% resistance=330 package=THT]
  KY-1 = Keyes Relay [package=THT]
  L1 = Solenoid
  Power_plug1 = Power plug

nets:
  N1: ESP32_-_Back1.GPIO2, R2.Pin_0, KY-1.signal
  N2: ESP32_-_Back1.GPIO14, R1.Pin_0
  GND: ESP32_-_Back1.GND, Componente1.GND, LED1.cathode, LED2.cathode, KY-1.ground
  N3: ESP32_-_Back1.5V, Componente1.POWER, KY-1.power
  N4: ESP32_-_Back1.GPIO3_/_RX, Componente1.TXO
  N5: ESP32_-_Back1.GPIO1_/_TX, Componente1.RXI
  N6: LED1.anode, R1.Pin_1
  N7: LED2.anode, R2.Pin_1
  N8: KY-1.C, Power_plug1.VCC
  N9: KY-1.NO, L1.pin2

custom parts:
  ESP32 - CAM: The ESP32-CAM has a very competitive small-size camera module that can operate independently as a minimum system with a footprint of only 27*40.5*4.5mm and a deep sleep current of up to 6mA.
  Keyes Relay: The Keyes 5V relay module is suitable for SCM development, home appliance control. It uses a 5V~12V TIL control signal which can control DC / AC signal.
