# Fritzing sketch controle_real_time2 (saved by Fritzing 0.9.4)
breadboards: 1

parts:
  ESP32_-_CAM = ESP32 - CAM
  CONVERSOR_SERIAL/USB = FTDI Basic Programmer
  LED1 = LED - 5mm [color="Red (633nm)" package="5 mm [THT]"]
  R1 = Resistor [tolerance=±5% resistance=330 package=THT]
  LED2 = LED - 5mm [color="Green (570nm)" package="5 mm [THT]"]
  R2 = Resistor [tolerance=±5% resistance=330 package=THT]
  MODULO_RELE = Keyes Relay [package=THT]
  L1 = Solenoid
  POWER = Power plug

nets:
  N1: ESP32_-_CAM.GPIO2, R2.Pin_0, MODULO_RELE.signal
  N2: ESP32_-_CAM.GPIO14, R1.Pin_0
  GND: ESP32_-_CAM.GND, CONVERSOR_SERIAL/USB.GND, LED1.cathode, LED2.cathode, MODULO_RELE.ground
  N3: ESP32_-_CAM.5V, CONVERSOR_SERIAL/USB.POWER, MODULO_RELE.power
  N4: ESP32_-_CAM.GPIO3_/_RX, CONVERSOR_SERIAL/USB.TXO
  N5: ESP32_-_CAM.GPIO1_/_TX, CONVERSOR_SERIAL/USB.RXI
  N6: LED1.anode, R1.Pin_1
  N7: LED2.anode, R2.Pin_1
  N8: MODULO_RELE.NC, MODULO_RELE.C, POWER.VCC
  N9: MODULO_RELE.NO, L1.pin2
  N10: L1.pin1, POWER.GND

custom parts:
  ESP32 - CAM: The ESP32-CAM has a very competitive small-size camera module that can operate independently as a minimum system with a footprint of only 27*40.5*4.5mm and a deep sleep current of up to 6mA.
  Keyes Relay: The Keyes 5V relay module is suitable for SCM development, home appliance control. It uses a 5V~12V TIL control signal which can control DC / AC signal.
